// Logisim project EIPE16.circ as structural Verilog: 7 circuits, main circuit EIPE16GP
module EIPE16GP (
  input  clk,
  input  [7:0] inst,
  input  useBuiltIn,
  input  reset,
  input  Interrupt,
  input  [15:0] Peripheral1,
  input  [15:0] Peripheral2,
  input  [15:0] Peripheral3,
  input  [15:0] Peripheral4,
  input  [15:0] GA,
  output AcceptClock,
  output RequestJump,
  output RequestWrite,
  output [15:0] WriteValue,
  output [15:0] P1,
  output Pout1,
  output [15:0] P2,
  output Pout2,
  output [15:0] P3,
  output Pout3,
  output [15:0] P4,
  output Pout4,
  output [15:0] GPU,
  output ClkOut
);

  wire and_1_out, and_2_out, and_4_out, and_5_out, and_6_out, and_7_out, and_8_out, and_9_out, and_10_out,
       and_11_out, bitselector_1_out, bitselector_8_out, BR_q, buffer_1_out, buffer_2_out,
       controlled_buffer_1_out, counter_2_carry, demultiplexer_1_out0, demultiplexer_1_out1,
       demultiplexer_1_out2, demultiplexer_1_out3, demultiplexer_1_out4, demultiplexer_1_out5,
       demultiplexer_1_out8, demultiplexer_1_out9, demultiplexer_1_out10, demultiplexer_1_out11,
       demultiplexer_1_out12, demultiplexer_1_out13, demultiplexer_1_out14, demultiplexer_1_out15,
       demultiplexer_1_out16, demultiplexer_1_out18, demultiplexer_1_out19, demultiplexer_1_out20,
       demultiplexer_1_out21, demultiplexer_1_out22, demultiplexer_1_out23, demultiplexer_1_out24,
       demultiplexer_1_out25, demultiplexer_1_out26, demultiplexer_1_out27, demultiplexer_1_out30,
       demultiplexer_1_out31, demultiplexer_2_out0, demultiplexer_2_out1, demultiplexer_2_out2,
       demultiplexer_2_out3, not_1_out, not_2_out, or_2_out, or_3_out, or_4_out, or_5_out, or_6_out,
       or_7_out, s_r_ff_1_qn, t_ff_1_q, t_ff_1_qn;
  wire [4:0] bitselector_2_out, bitselector_4_out, bitselector_5_out, bitselector_6_out, bitselector_7_out,
       bitselector_9_out, bitselector_10_out;
  wire [7:0] adder_1_out, counter_3_q, DebugInst_data, InstructionChip_data, InstructionLUT_data,
       multiplexer_1_out;
  wire [15:0] alu_1_carry, alu_1_out_4, bitselector_3_out, CARRY_q, counter_1_q, counter_4_q,
       demultiplexer_3_out0, demultiplexer_3_out1, demultiplexer_3_out2, demultiplexer_3_out3,
       demultiplexer_3_out5, multiplexer_2_out, multiplexer_5_out, nand_1_out, register_1_q, register_2_q,
       register_3_q, register_4_q, Stack_dout;
  wire [47:0] shift_register_1_out;

  buf buffer_1 (buffer_1_out, clk);
  buf buffer_2 (buffer_2_out, buffer_1_out);
  assign controlled_buffer_1_out = reset ? reset : 1'bz;  // Controlled_Buffer controlled_buffer_1
  not not_1 (not_1_out, reset);
  assign controlled_buffer_1_out = not_1_out ? Interrupt : 1'bz;  // Controlled_Buffer controlled_buffer_2
  Counter #(.max('hffff), .trigger("falling"), .width(16)) counter_1 (
    .count(t_ff_1_qn), .Q(counter_1_q), .clk(and_1_out), .clr(reset));  // open: load, D, carry, up
  and and_1 (and_1_out, clk, s_r_ff_1_qn);
  not not_2 (not_2_out, buffer_2_out);
  ROM #(.addrWidth(16)) DebugInst (.addr(counter_1_q), .data(DebugInst_data));
  S_R_Flip_Flop s_r_ff_1 (
    .S(demultiplexer_1_out22), .clk(not_2_out), .R(controlled_buffer_1_out), .Qn(s_r_ff_1_qn),
    .reset(controlled_buffer_1_out));  // open: Q, preset
  and and_2 (and_2_out, demultiplexer_1_out12, bitselector_1_out);
  and and_3 (AcceptClock, t_ff_1_qn, s_r_ff_1_qn);
  and and_4 (and_4_out, demultiplexer_1_out10, BR_q);
  and and_5 (and_5_out, demultiplexer_1_out11, ~bitselector_1_out);  // AND_Gate
  or or_1 (RequestJump, demultiplexer_1_out18, demultiplexer_1_out21, and_2_out, and_5_out, demultiplexer_1_out20, and_4_out, and_6_out, demultiplexer_1_out13, RequestWrite);
  and and_6 (and_6_out, demultiplexer_1_out9, ~BR_q);  // AND_Gate
  Multiplexer #(.width(8)) multiplexer_1 (.in0(inst), .in1(DebugInst_data), .out(multiplexer_1_out), .sel(useBuiltIn));
  Counter #(.max('h5), .trigger("falling")) counter_2 (
    .count(t_ff_1_qn), .carry(counter_2_carry), .clk(and_1_out), .clr(and_7_out));  // open: load, D, Q, up
  ROM InstructionLUT (.addr(shift_register_1_out[7:0]), .data(InstructionLUT_data));
  ROM InstructionChip (.addr(adder_1_out), .data(InstructionChip_data));
  Adder adder_1 (.a(InstructionLUT_data), .b(counter_3_q), .out(adder_1_out));  // open: cin, cout
  assign nand_1_out = ~({16{1'b0}} & CARRY_q);  // NAND_Gate nand_1, 16 bits wide
  BitSelector #(.width(16)) bitselector_1 (.in(nand_1_out), .out(bitselector_1_out), .sel(4'b1111));
  Counter #(.ongoal("stay")) counter_3 (
    .count(t_ff_1_q), .Q(counter_3_q), .clk(and_1_out), .clr(t_ff_1_qn));  // open: load, D, carry, up
  Demultiplexer #(.select(5)) demultiplexer_1 (
    .out0(demultiplexer_1_out0), .out1(demultiplexer_1_out1), .out2(demultiplexer_1_out2),
    .out3(demultiplexer_1_out3), .out4(demultiplexer_1_out4), .out5(demultiplexer_1_out5),
    .out8(demultiplexer_1_out8), .out9(demultiplexer_1_out9), .out10(demultiplexer_1_out10),
    .out11(demultiplexer_1_out11), .out12(demultiplexer_1_out12), .out13(demultiplexer_1_out13),
    .out14(demultiplexer_1_out14), .out15(demultiplexer_1_out15), .out16(demultiplexer_1_out16),
    .out17(RequestWrite), .out18(demultiplexer_1_out18), .out19(demultiplexer_1_out19),
    .out20(demultiplexer_1_out20), .out21(demultiplexer_1_out21), .out22(demultiplexer_1_out22),
    .out23(demultiplexer_1_out23), .out24(demultiplexer_1_out24), .out25(demultiplexer_1_out25),
    .out26(demultiplexer_1_out26), .out27(demultiplexer_1_out27), .out30(demultiplexer_1_out30),
    .out31(demultiplexer_1_out31), .in(1'b1), .sel(bitselector_2_out));  // open: out6, out7, out28, out29
  BitSelector #(.group(5)) bitselector_2 (.in(InstructionChip_data), .out(bitselector_2_out), .sel(1'b0));
  and and_7 (and_7_out, demultiplexer_1_out30, and_1_out);
  // Probe on shift_register_1_out
  T_Flip_Flop #(.trigger("falling")) t_ff_1 (
    .clk(and_8_out), .Q(t_ff_1_q), .Qn(t_ff_1_qn), .preset(demultiplexer_1_out31), .reset(and_7_out));  // open: T
  Shift_Register #(.length(6), .width(8)) shift_register_1 (
    .shift(t_ff_1_qn), .in(multiplexer_1_out), .clk(and_1_out), .out(shift_register_1_out[7:0]), .clr(reset),
    .q0(shift_register_1_out[47:40]), .q1(shift_register_1_out[39:32]), .q2(shift_register_1_out[31:24]),
    .q3(shift_register_1_out[23:16]), .q4(shift_register_1_out[15:8]));  // open: load, d0, d1, d2, d3, d4, d5, q5
  and and_8 (and_8_out, counter_2_carry, and_1_out);
  BitSelector #(.group(16), .width(1)) bitselector_3 (.in(BR_q), .out(bitselector_3_out), .sel(1'b0));
  delayer D1 (.in_1(and_8_out), .in_2(3'b101), .out_3(ClkOut));
  Multiplexer #(.select(5), .width(16)) multiplexer_2 (
    .in0(register_1_q), .in1(register_2_q), .in2(register_3_q), .in3(register_4_q), .in4(CARRY_q),
    .in5(bitselector_3_out), .in6(GA), .in7(Peripheral1), .in8(Peripheral2), .in9(Peripheral3),
    .in10(Peripheral4), .in11(counter_4_q),
    .in18({shift_register_1_out[39:32], shift_register_1_out[47:40]}), .out(multiplexer_2_out),
    .sel(bitselector_4_out));  // open: in12, in13, in14, in15, in16, in17, in19, in20, in21, in22, in23, in24, in25, in26, in27, in28, in29, in30, in31
  BitSelector #(.group(5)) bitselector_4 (.in(shift_register_1_out[15:8]), .out(bitselector_4_out), .sel(1'b0));
  Multiplexer #(.select(5), .width(16)) multiplexer_3 (
    .in0(register_1_q), .in1(register_2_q), .in2(register_3_q), .in3(register_4_q), .in4(CARRY_q), .in6(GA),
    .in7(Peripheral1), .in8(Peripheral2), .in9(Peripheral3), .in10(Peripheral4), .in11(counter_4_q),
    .in18({shift_register_1_out[39:32], shift_register_1_out[47:40]}), .out(WriteValue),
    .sel(bitselector_5_out));  // open: in5, in12, in13, in14, in15, in16, in17, in19, in20, in21, in22, in23, in24, in25, in26, in27, in28, in29, in30, in31
  BitSelector #(.group(5)) bitselector_5 (.in(shift_register_1_out[23:16]), .out(bitselector_5_out), .sel(1'b0));
  or or_2 (or_2_out, demultiplexer_1_out0, demultiplexer_1_out1, demultiplexer_1_out2, demultiplexer_1_out3, demultiplexer_1_out4, demultiplexer_1_out5, demultiplexer_1_out8, demultiplexer_1_out14, demultiplexer_1_out15, demultiplexer_1_out16, demultiplexer_1_out18, demultiplexer_1_out19, demultiplexer_1_out24, demultiplexer_1_out25, demultiplexer_1_out26, demultiplexer_1_out27);
  Demultiplexer #(.select(5)) demultiplexer_2 (
    .out0(demultiplexer_2_out0), .out1(demultiplexer_2_out1), .out2(demultiplexer_2_out2),
    .out3(demultiplexer_2_out3), .out7(Pout1), .out8(Pout2), .out9(Pout3), .out10(Pout4), .in(or_2_out),
    .sel(bitselector_7_out));  // open: out4, out5, out6, out11, out12, out13, out14, out15, out16, out17, out18, out19, out20, out21, out22, out23, out24, out25, out26, out27, out28, out29, out30, out31
  Register #(.width(16)) register_1 (
    .D(demultiplexer_3_out0), .en(demultiplexer_2_out0), .Q(register_1_q), .clk(ClkOut), .clr(reset));
  BitSelector #(.group(5)) bitselector_6 (.in(InstructionChip_data), .out(bitselector_6_out), .sel(1'b0));
  BitSelector #(.group(5)) bitselector_7 (.in(shift_register_1_out[31:24]), .out(bitselector_7_out), .sel(1'b0));
  Register #(.width(16)) register_2 (
    .D(demultiplexer_3_out1), .en(demultiplexer_2_out1), .Q(register_2_q), .clk(ClkOut), .clr(reset));
  ALU alu_1 (
    .Operand1(multiplexer_2_out), .Operand2(WriteValue), .Inst(bitselector_6_out), .out_4(alu_1_out_4),
    .Carry(alu_1_carry));
  or or_3 (or_3_out, and_9_out, and_10_out);
  and and_9 (and_9_out, and_8_out, or_7_out);
  Register #(.width(16)) register_3 (
    .D(demultiplexer_3_out2), .en(demultiplexer_2_out2), .Q(register_3_q), .clk(ClkOut), .clr(reset));
  and and_10 (and_10_out, or_5_out, and_11_out);
  Register #(.width(16)) register_4 (
    .D(demultiplexer_3_out3), .en(demultiplexer_2_out3), .Q(register_4_q), .clk(ClkOut), .clr(reset));
  Multiplexer #(.width(16)) multiplexer_4 (
    .in0(multiplexer_2_out), .in1(Stack_dout), .out(P1), .sel(demultiplexer_1_out21));
  or or_4 (or_4_out, or_5_out, or_7_out);
  or or_5 (or_5_out, demultiplexer_1_out30, demultiplexer_1_out20);
  or or_6 (or_6_out, demultiplexer_1_out23, demultiplexer_1_out3, demultiplexer_1_out0, demultiplexer_1_out4);
  BitSelector #(.width(16)) bitselector_8 (.in(demultiplexer_3_out5), .out(bitselector_8_out), .sel(4'b0000));
  Register #(.width(16)) CARRY (.D(alu_1_carry), .en(or_6_out), .Q(CARRY_q), .clk(ClkOut), .clr(reset));
  Counter #(.max('hffff), .width(16)) counter_4 (
    .count(or_4_out), .Q(counter_4_q), .up(or_5_out), .clk(or_3_out));  // open: load, D, carry, clr
  RAM #(.addrWidth(16), .dataWidth(16), .enables("line")) Stack (
    .addr(counter_4_q), .we(or_5_out), .clk(and_11_out), .din(multiplexer_2_out), .dout(Stack_dout));
  and and_11 (and_11_out, and_8_out, or_4_out);
  or or_7 (or_7_out, demultiplexer_1_out21, demultiplexer_1_out8);
  Register #(.width(1)) BR (.D(bitselector_8_out), .Q(BR_q), .clk(ClkOut), .clr(reset));  // open: en
  Demultiplexer #(.select(5), .width(16)) demultiplexer_3 (
    .out0(demultiplexer_3_out0), .out1(demultiplexer_3_out1), .out2(demultiplexer_3_out2),
    .out3(demultiplexer_3_out3), .out5(demultiplexer_3_out5), .out6(GPU), .out7(P1), .out8(P2), .out9(P3),
    .out10(P4), .in(multiplexer_5_out), .sel(bitselector_10_out));  // open: out4, out11, out12, out13, out14, out15, out16, out17, out18, out19, out20, out21, out22, out23, out24, out25, out26, out27, out28, out29, out30, out31
  Multiplexer #(.select(5), .width(16)) multiplexer_5 (
    .in0(alu_1_out_4), .in1(alu_1_out_4), .in2(alu_1_out_4), .in3(alu_1_out_4), .in8(Stack_dout),
    .in14(alu_1_out_4), .in15(alu_1_out_4), .in16(alu_1_out_4), .in19(multiplexer_2_out),
    .out(multiplexer_5_out), .sel(bitselector_9_out));  // open: in4, in5, in6, in7, in9, in10, in11, in12, in13, in17, in18, in20, in21, in22, in23, in24, in25, in26, in27, in28, in29, in30, in31
  BitSelector #(.group(5)) bitselector_9 (.in(InstructionChip_data), .out(bitselector_9_out), .sel(1'b0));
  BitSelector #(.group(5)) bitselector_10 (.in(shift_register_1_out[31:24]), .out(bitselector_10_out), .sel(1'b0));

  // Notes on the sheet:
  //   EIPE 16 GP
  //   8 bit inst
  //   8 bit operand 1
  //   8 bit operand 2
  //   8 bit output
  //   16 bit imm
  //   Debug, can be removed
  //   contents of DebugInst (hex, n*v repeats v):
  //   16
  //   contents of InstructionLUT (hex, n*v repeats v):
  //   0 1 2 3 4 5 6 7 8 9 a b c d e f 10 11 16 17 18 19 1a 1b 1c 1d 1e 1f 20 21 22 23 20 21 22 23 24 25
  //   contents of InstructionChip (hex, n*v repeats v):
  //   0 1 2 3 4 5 6 7 8 9 a b c d e f 10 1f 14 11 15 1e 12 13 14 15 16 17 18 19 1a 1b 1c 1d 1e 1f
  //   Branching Handler
endmodule

module ALU (
  input  [15:0] Operand1,
  input  [15:0] Operand2,
  input  [4:0] Inst,
  output [15:0] out_4,
  output [15:0] Carry
);

  wire adder_1_cout, subtractor_1_bout;
  wire [3:0] bitselector_1_out;
  wire [15:0] adder_1_out, and_1_out, bitselector_2_out, bitselector_3_out, multiplier_1_cout,
       multiplier_1_out, nand_1_out, shifter_1_out, shifter_2_out, shifter_3_out, shifter_4_out,
       subtractor_1_out, xor_1_out;

  assign and_1_out = Operand1 & Operand2;  // AND_Gate and_1, 16 bits wide
  BitSelector #(.group(4), .width(16)) bitselector_1 (.in(Operand2), .out(bitselector_1_out), .sel(2'b00));
  Adder #(.width(16)) adder_1 (.a(Operand1), .b(Operand2), .out(adder_1_out), .cout(adder_1_cout));  // open: cin
  Subtractor #(.width(16)) subtractor_1 (
    .a(Operand1), .b(Operand2), .out(subtractor_1_out), .bout(subtractor_1_bout));  // open: bin
  assign nand_1_out = ~(Operand1 & Operand2);  // NAND_Gate nand_1, 16 bits wide
  Multiplier #(.width(16)) multiplier_1 (
    .a(Operand1), .b(Operand2), .out(multiplier_1_out), .cout(multiplier_1_cout));  // open: cin
  assign xor_1_out = Operand1 ^ Operand2;  // XOR_Gate xor_1, 16 bits wide
  Shifter #(.width(16)) shifter_1 (.in(Operand1), .\dist (bitselector_1_out), .out(shifter_1_out));
  Shifter #(.shift("rl"), .width(16)) shifter_2 (.in(Operand1), .\dist (bitselector_1_out), .out(shifter_2_out));
  Shifter #(.shift("lr"), .width(16)) shifter_3 (.in(Operand1), .\dist (bitselector_1_out), .out(shifter_3_out));
  Shifter #(.shift("rr"), .width(16)) shifter_4 (.in(Operand1), .\dist (bitselector_1_out), .out(shifter_4_out));
  BitSelector #(.group(16), .width(1)) bitselector_2 (.in(adder_1_cout), .out(bitselector_2_out), .sel(1'b0));
  BitSelector #(.group(16), .width(1)) bitselector_3 (.in(subtractor_1_bout), .out(bitselector_3_out), .sel(1'b0));
  Multiplexer #(.select(5), .width(16)) multiplexer_1 (
    .in0(adder_1_out), .in1(adder_1_out), .in2(subtractor_1_out), .in3(subtractor_1_out),
    .in4(multiplier_1_out), .in5(multiplier_1_out), .in14(and_1_out), .in15(nand_1_out), .in16(xor_1_out),
    .in23(shifter_1_out), .in24(shifter_2_out), .in25(shifter_3_out), .in26(shifter_4_out), .out(out_4),
    .sel(Inst));  // open: in6, in7, in8, in9, in10, in11, in12, in13, in17, in18, in19, in20, in21, in22, in27, in28, in29, in30, in31
  Multiplexer #(.select(5), .width(16)) multiplexer_2 (
    .in0(bitselector_2_out), .in3(bitselector_3_out), .in5(multiplier_1_cout), .in23(bitselector_3_out),
    .out(Carry), .sel(Inst));  // open: in1, in2, in4, in6, in7, in8, in9, in10, in11, in12, in13, in14, in15, in16, in17, in18, in19, in20, in21, in22, in24, in25, in26, in27, in28, in29, in30, in31
endmodule

module Motherboard (
);

  wire button_1_out, button_2_out, clock_1_out, eipe16gp_1_acceptclock, eipe16gp_1_clkout, eipe16gp_1_pout1,
       eipe16gp_1_pout2, eipe16gp_1_pout3, eipe16gp_1_requestjump, eipe16gp_1_requestwrite,
       memorymanager_1_chipwrite2;
  wire [3:0] eipe16gp_1_p3_2, eipe16gp_1_p3_3;
  wire [6:0] bitselector_2_out, keyboard_1_data;
  wire [7:0] bitselector_1_out, eipe16gp_1_p3, memorymanager_1_chipd2, memorymanager_1_dataout, ram_1_dout,
       rom_1_data;
  wire [14:0] memorymanager_1_chipa1, memorymanager_1_chipa2;
  wire [15:0] bitselector_3_out, counter_1_q, eipe16gp_1_p1, eipe16gp_1_writevalue;

  ROM #(.addrWidth(15)) rom_1 (.addr(memorymanager_1_chipa1), .data(rom_1_data));
  Clock clock_1 (.out(clock_1_out));
  Button button_1 (.out(button_1_out));
  Counter #(.max('hffff), .trigger("falling"), .width(16)) counter_1 (
    .load(eipe16gp_1_requestjump), .D(eipe16gp_1_writevalue), .count(eipe16gp_1_acceptclock),
    .Q(counter_1_q), .clk(clock_1_out));  // open: carry, up, clr
  Button button_2 (.out(button_2_out));
  RAM #(.addrWidth(15), .enables("line")) ram_1 (
    .addr(memorymanager_1_chipa2), .we(memorymanager_1_chipwrite2), .clk(eipe16gp_1_clkout),
    .din(memorymanager_1_chipd2), .dout(ram_1_dout));
  MemoryManager memorymanager_1 (
    .Address(counter_1_q), .WriteRq(eipe16gp_1_requestwrite), .Data(bitselector_1_out),
    .ChipDataIn1(rom_1_data), .ChipDataIn2(ram_1_dout), .ChipA1(memorymanager_1_chipa1),
    .ChipA2(memorymanager_1_chipa2), .ChipD2(memorymanager_1_chipd2),
    .ChipWrite2(memorymanager_1_chipwrite2), .DataOut(memorymanager_1_dataout));  // open: ChipD1, ChipWrite1
  EIPE16GP eipe16gp_1 (
    .clk(clock_1_out), .inst(memorymanager_1_dataout), .useBuiltIn(1'b0), .reset(button_2_out),
    .Interrupt(button_1_out), .Peripheral1(bitselector_3_out), .AcceptClock(eipe16gp_1_acceptclock),
    .RequestJump(eipe16gp_1_requestjump), .RequestWrite(eipe16gp_1_requestwrite),
    .WriteValue(eipe16gp_1_writevalue), .P1(eipe16gp_1_p1), .Pout1(eipe16gp_1_pout1),
    .Pout2(eipe16gp_1_pout2), .P3({eipe16gp_1_p3_3, eipe16gp_1_p3_2, eipe16gp_1_p3}),
    .Pout3(eipe16gp_1_pout3), .ClkOut(eipe16gp_1_clkout));  // open: Peripheral2, Peripheral3, Peripheral4, GA, P2, P4, Pout4, GPU
  BitSelector #(.group(8), .width(16)) bitselector_1 (.in(eipe16gp_1_writevalue), .out(bitselector_1_out), .sel(1'b0));
  TTY tty_1 (.data(bitselector_2_out), .clk(eipe16gp_1_clkout), .we(eipe16gp_1_pout1));  // open: clr
  BitSelector #(.group(7), .width(16)) bitselector_2 (.in(eipe16gp_1_p1), .out(bitselector_2_out), .sel(2'b00));
  BitSelector #(.group(16), .width(7)) bitselector_3 (.in(keyboard_1_data), .out(bitselector_3_out), .sel(1'b0));
  Keyboard keyboard_1 (.clk(eipe16gp_1_clkout), .re(eipe16gp_1_pout2), .data(keyboard_1_data));  // open: clr, avail
  // RGB_Video #(.height(16), .scale(8), .width(16)) rgb_video_1: pin names not known; wires that end beside it: eipe16gp_1_clkout, eipe16gp_1_pout3, eipe16gp_1_p3_3, eipe16gp_1_p3_2, eipe16gp_1_p3

  // Notes on the sheet:
  //   contents of rom_1 (hex, n*v repeats v):
  //   10*0 80
endmodule

module MemoryManager (
  input  [15:0] Address,
  input  WriteRq,
  input  [7:0] Data,
  input  [7:0] ChipDataIn1,
  input  [7:0] ChipDataIn2,
  output [14:0] ChipA1,
  output [7:0] ChipD1,
  output ChipWrite1,
  output [14:0] ChipA2,
  output [7:0] ChipD2,
  output ChipWrite2,
  output [7:0] DataOut
);

  // Probe on Address
  // Probe on Address
  Demultiplexer #(.width(15)) demultiplexer_1 (.out0(ChipA1), .out1(ChipA2), .in(Address[14:0]), .sel(Address[15]));
  Demultiplexer demultiplexer_2 (.out0(ChipWrite1), .out1(ChipWrite2), .in(WriteRq), .sel(Address[15]));
  Demultiplexer #(.width(8)) demultiplexer_3 (.out0(ChipD1), .in(Data), .sel(Address[15]));  // open: out1
  Multiplexer #(.width(8)) multiplexer_1 (.in0(ChipDataIn1), .in1(ChipDataIn2), .out(DataOut), .sel(Address[15]));

  assign ChipD2 = ChipD1;

  // Notes on the sheet:
  //   TODO:
  //   Add the ability to have values bigger than 16 bits support
endmodule

module RenderCore (
  input  [7:0] Inst,
  input  [7:0] PxPos,
  input  [7:0] PxColor,
  output [7:0] PxColorOut
);
endmodule

module GPU (
  input  [15:0] dIn,
  input  CLK
);

  wire [7:0] Pallete_dout;

  RAM #(.enables("line")) VRAM (.clk(CLK));  // open: addr, we, din, dout
  RAM #(.enables("line")) Pallete (.clk(CLK), .dout(Pallete_dout));  // open: addr, we, din
  RAM #(.enables("line")) Buffer1 (.clk(CLK), .din(Pallete_dout));  // open: addr, we, dout
  RAM #(.enables("line")) Buffer2 (.clk(CLK), .din(Pallete_dout));  // open: addr, we, dout
endmodule

module delayer (
  input  in_1,
  input  [2:0] in_2,
  output out_3
);

  wire buffer_1_out, buffer_2_out, buffer_3_out, buffer_4_out, buffer_5_out, buffer_6_out, buffer_7_out,
       buffer_8_out, buffer_9_out, buffer_10_out, buffer_11_out, buffer_12_out, buffer_13_out, buffer_14_out,
       buffer_15_out, buffer_16_out, buffer_17_out, buffer_18_out, buffer_19_out, buffer_20_out,
       buffer_21_out, buffer_22_out, buffer_23_out, buffer_24_out, buffer_25_out, buffer_26_out,
       buffer_27_out, buffer_28_out, buffer_29_out, buffer_30_out, buffer_31_out, buffer_32_out,
       buffer_33_out, buffer_34_out, buffer_35_out, buffer_36_out, buffer_37_out, buffer_38_out,
       buffer_39_out, buffer_40_out, buffer_41_out, buffer_42_out, buffer_43_out, buffer_44_out,
       buffer_45_out, buffer_46_out, buffer_47_out, buffer_48_out, buffer_49_out, buffer_50_out,
       buffer_51_out, buffer_52_out, buffer_53_out, buffer_54_out, buffer_55_out, buffer_56_out,
       buffer_57_out, buffer_58_out, buffer_59_out, buffer_60_out, buffer_61_out, buffer_62_out,
       buffer_63_out, buffer_64_out, buffer_65_out, buffer_66_out, buffer_67_out, buffer_68_out,
       buffer_69_out, buffer_70_out, buffer_71_out, buffer_72_out, buffer_73_out, buffer_74_out,
       buffer_75_out, buffer_76_out, buffer_77_out, buffer_78_out, buffer_79_out, buffer_80_out,
       buffer_81_out, buffer_82_out, buffer_83_out, buffer_84_out, buffer_85_out, buffer_86_out,
       buffer_87_out, buffer_88_out, buffer_89_out, buffer_90_out, buffer_91_out, buffer_92_out,
       buffer_93_out, buffer_94_out, buffer_95_out, buffer_96_out, buffer_97_out, buffer_98_out,
       buffer_99_out, buffer_100_out, buffer_101_out, buffer_102_out, buffer_103_out, buffer_104_out,
       buffer_105_out, buffer_106_out, buffer_107_out, buffer_108_out, buffer_109_out, buffer_110_out,
       buffer_111_out, buffer_112_out, buffer_113_out, buffer_114_out, buffer_115_out, buffer_116_out,
       buffer_117_out, buffer_118_out, buffer_119_out, buffer_120_out;

  buf buffer_1 (buffer_1_out, buffer_3_out);
  buf buffer_2 (buffer_2_out, buffer_5_out);
  buf buffer_3 (buffer_3_out, buffer_7_out);
  buf buffer_4 (buffer_4_out, buffer_1_out);
  buf buffer_5 (buffer_5_out, buffer_9_out);
  buf buffer_6 (buffer_6_out, buffer_2_out);
  buf buffer_7 (buffer_7_out, buffer_11_out);
  buf buffer_8 (buffer_8_out, buffer_4_out);
  buf buffer_9 (buffer_9_out, buffer_13_out);
  buf buffer_10 (buffer_10_out, buffer_6_out);
  buf buffer_11 (buffer_11_out, buffer_15_out);
  buf buffer_12 (buffer_12_out, buffer_8_out);
  buf buffer_13 (buffer_13_out, buffer_17_out);
  buf buffer_14 (buffer_14_out, buffer_10_out);
  buf buffer_15 (buffer_15_out, buffer_19_out);
  buf buffer_16 (buffer_16_out, buffer_12_out);
  buf buffer_17 (buffer_17_out, buffer_21_out);
  buf buffer_18 (buffer_18_out, buffer_14_out);
  buf buffer_19 (buffer_19_out, buffer_23_out);
  buf buffer_20 (buffer_20_out, buffer_16_out);
  buf buffer_21 (buffer_21_out, buffer_25_out);
  buf buffer_22 (buffer_22_out, buffer_18_out);
  buf buffer_23 (buffer_23_out, buffer_27_out);
  buf buffer_24 (buffer_24_out, buffer_20_out);
  buf buffer_25 (buffer_25_out, buffer_29_out);
  buf buffer_26 (buffer_26_out, buffer_22_out);
  buf buffer_27 (buffer_27_out, buffer_31_out);
  buf buffer_28 (buffer_28_out, buffer_24_out);
  buf buffer_29 (buffer_29_out, buffer_33_out);
  buf buffer_30 (buffer_30_out, buffer_26_out);
  buf buffer_31 (buffer_31_out, buffer_35_out);
  buf buffer_32 (buffer_32_out, buffer_28_out);
  buf buffer_33 (buffer_33_out, buffer_37_out);
  buf buffer_34 (buffer_34_out, buffer_30_out);
  buf buffer_35 (buffer_35_out, buffer_39_out);
  buf buffer_36 (buffer_36_out, buffer_32_out);
  buf buffer_37 (buffer_37_out, buffer_41_out);
  buf buffer_38 (buffer_38_out, buffer_34_out);
  buf buffer_39 (buffer_39_out, buffer_43_out);
  buf buffer_40 (buffer_40_out, buffer_36_out);
  buf buffer_41 (buffer_41_out, buffer_45_out);
  buf buffer_42 (buffer_42_out, buffer_38_out);
  buf buffer_43 (buffer_43_out, buffer_47_out);
  buf buffer_44 (buffer_44_out, buffer_40_out);
  buf buffer_45 (buffer_45_out, buffer_49_out);
  buf buffer_46 (buffer_46_out, buffer_42_out);
  buf buffer_47 (buffer_47_out, buffer_51_out);
  buf buffer_48 (buffer_48_out, buffer_44_out);
  buf buffer_49 (buffer_49_out, buffer_53_out);
  buf buffer_50 (buffer_50_out, buffer_46_out);
  buf buffer_51 (buffer_51_out, buffer_55_out);
  buf buffer_52 (buffer_52_out, buffer_48_out);
  buf buffer_53 (buffer_53_out, buffer_57_out);
  buf buffer_54 (buffer_54_out, buffer_50_out);
  buf buffer_55 (buffer_55_out, buffer_59_out);
  buf buffer_56 (buffer_56_out, buffer_52_out);
  buf buffer_57 (buffer_57_out, buffer_61_out);
  buf buffer_58 (buffer_58_out, buffer_54_out);
  buf buffer_59 (buffer_59_out, buffer_63_out);
  buf buffer_60 (buffer_60_out, buffer_56_out);
  buf buffer_61 (buffer_61_out, buffer_65_out);
  buf buffer_62 (buffer_62_out, buffer_58_out);
  buf buffer_63 (buffer_63_out, buffer_67_out);
  buf buffer_64 (buffer_64_out, buffer_60_out);
  buf buffer_65 (buffer_65_out, buffer_69_out);
  buf buffer_66 (buffer_66_out, buffer_62_out);
  buf buffer_67 (buffer_67_out, buffer_71_out);
  buf buffer_68 (buffer_68_out, buffer_64_out);
  buf buffer_69 (buffer_69_out, buffer_73_out);
  buf buffer_70 (buffer_70_out, buffer_66_out);
  buf buffer_71 (buffer_71_out, buffer_75_out);
  buf buffer_72 (buffer_72_out, buffer_68_out);
  buf buffer_73 (buffer_73_out, buffer_77_out);
  buf buffer_74 (buffer_74_out, buffer_70_out);
  buf buffer_75 (buffer_75_out, in_1);
  buf buffer_76 (buffer_76_out, buffer_72_out);
  buf buffer_77 (buffer_77_out, buffer_79_out);
  buf buffer_78 (buffer_78_out, buffer_74_out);
  buf buffer_79 (buffer_79_out, buffer_76_out);
  buf buffer_80 (buffer_80_out, buffer_78_out);
  buf buffer_81 (buffer_81_out, buffer_82_out);
  buf buffer_82 (buffer_82_out, buffer_84_out);
  buf buffer_83 (buffer_83_out, buffer_81_out);
  buf buffer_84 (buffer_84_out, buffer_86_out);
  buf buffer_85 (buffer_85_out, buffer_83_out);
  buf buffer_86 (buffer_86_out, buffer_88_out);
  buf buffer_87 (buffer_87_out, buffer_85_out);
  buf buffer_88 (buffer_88_out, buffer_90_out);
  buf buffer_89 (buffer_89_out, buffer_87_out);
  buf buffer_90 (buffer_90_out, buffer_92_out);
  buf buffer_91 (buffer_91_out, buffer_89_out);
  buf buffer_92 (buffer_92_out, buffer_94_out);
  buf buffer_93 (buffer_93_out, buffer_91_out);
  buf buffer_94 (buffer_94_out, buffer_96_out);
  buf buffer_95 (buffer_95_out, buffer_93_out);
  buf buffer_96 (buffer_96_out, buffer_98_out);
  buf buffer_97 (buffer_97_out, buffer_95_out);
  buf buffer_98 (buffer_98_out, buffer_100_out);
  buf buffer_99 (buffer_99_out, buffer_97_out);
  buf buffer_100 (buffer_100_out, buffer_102_out);
  buf buffer_101 (buffer_101_out, buffer_99_out);
  buf buffer_102 (buffer_102_out, buffer_104_out);
  buf buffer_103 (buffer_103_out, buffer_101_out);
  buf buffer_104 (buffer_104_out, buffer_106_out);
  buf buffer_105 (buffer_105_out, buffer_103_out);
  buf buffer_106 (buffer_106_out, buffer_108_out);
  buf buffer_107 (buffer_107_out, buffer_105_out);
  buf buffer_108 (buffer_108_out, buffer_110_out);
  buf buffer_109 (buffer_109_out, buffer_107_out);
  buf buffer_110 (buffer_110_out, buffer_112_out);
  buf buffer_111 (buffer_111_out, buffer_109_out);
  buf buffer_112 (buffer_112_out, buffer_114_out);
  buf buffer_113 (buffer_113_out, buffer_111_out);
  buf buffer_114 (buffer_114_out, buffer_116_out);
  buf buffer_115 (buffer_115_out, buffer_113_out);
  buf buffer_116 (buffer_116_out, buffer_118_out);
  buf buffer_117 (buffer_117_out, buffer_115_out);
  buf buffer_118 (buffer_118_out, buffer_80_out);
  buf buffer_119 (buffer_119_out, buffer_117_out);
  buf buffer_120 (buffer_120_out, buffer_119_out);
  Multiplexer #(.select(3)) multiplexer_1 (
    .in0(buffer_1_out), .in1(buffer_79_out), .in2(buffer_2_out), .in3(buffer_80_out), .in4(buffer_81_out),
    .in5(buffer_120_out), .out(out_3), .sel(in_2));  // open: in6, in7

  // Notes on the sheet:
  //   Do not stare directly at the tower
endmodule
